// Logisim project Assignment1.circ as structural Verilog: 4 circuits, main circuit main
module main (
  input  Set_Time,
  input  in_2,
  input  in_3,
  input  in_4,
  input  in_5,
  input  in_6
);

  wire and_1_out, and_2_out, and_3_out, and_4_out, and_5_out, and_6_out, and_7_out, and_8_out, and_9_out,
       and_10_out, and_11_out, and_12_out, and_13_out, and_14_out, and_15_out, and_16_out, button_1_out,
       button_2_out, clock_1_out, j_k_ff_1_q, j_k_ff_2_q, j_k_ff_3_q, j_k_ff_4_q, j_k_ff_5_q, j_k_ff_6_q,
       j_k_ff_7_q, j_k_ff_8_q, j_k_ff_9_q, j_k_ff_9_qn, j_k_ff_10_q, j_k_ff_11_q, j_k_ff_12_q, j_k_ff_12_qn,
       not_1_out, or_1_out, or_2_out, or_3_out, or_4_out, or_5_out, or_6_out, t_ff_1_q;
  wire [0:0] d_ff_5_q;
  wire [2:0] d_ff_10_q;
  wire [3:0] d_ff_1_q, d_ff_6_q;

  J_K_Flip_Flop j_k_ff_1 (.J(in_2), .K(in_2), .clk(or_5_out), .Q(j_k_ff_1_q));  // open: Qn, preset, reset
  J_K_Flip_Flop j_k_ff_2 (
    .J(j_k_ff_1_q), .K(j_k_ff_1_q), .clk(or_5_out), .Q(j_k_ff_2_q), .reset(or_1_out));  // open: Qn, preset
  J_K_Flip_Flop j_k_ff_3 (
    .J(and_1_out), .K(and_1_out), .clk(or_5_out), .Q(j_k_ff_3_q), .reset(or_1_out));  // open: Qn, preset
  J_K_Flip_Flop j_k_ff_4 (
    .J(and_2_out), .K(and_2_out), .clk(or_5_out), .Q(j_k_ff_4_q), .reset(or_1_out));  // open: Qn, preset
  and and_1 (and_1_out, j_k_ff_4_q, and_2_out);
  and and_2 (and_2_out, j_k_ff_2_q, j_k_ff_1_q);
  LED led_1 (.in(j_k_ff_1_q));
  LED led_2 (.in(j_k_ff_2_q));
  LED led_3 (.in(j_k_ff_4_q));
  LED led_4 (.in(j_k_ff_3_q));
  and and_3 (and_3_out, j_k_ff_2_q, j_k_ff_3_q);
  D_Flip_Flop d_ff_1 (.D(j_k_ff_1_q), .clk(or_2_out), .Q(d_ff_1_q[0]));  // open: Qn, preset, reset
  D_Flip_Flop d_ff_2 (.D(j_k_ff_2_q), .clk(or_2_out), .Q(d_ff_1_q[1]));  // open: Qn, preset, reset
  or or_1 (or_1_out, and_3_out, and_4_out);
  J_K_Flip_Flop j_k_ff_5 (.J(in_2), .K(in_2), .clk(and_3_out), .Q(j_k_ff_5_q), .reset(and_4_out));  // open: Qn, preset
  D_Flip_Flop d_ff_3 (.D(j_k_ff_4_q), .clk(or_2_out), .Q(d_ff_1_q[2]));  // open: Qn, preset, reset
  D_Flip_Flop d_ff_4 (.D(j_k_ff_3_q), .clk(or_2_out), .Q(d_ff_1_q[3]));  // open: Qn, preset, reset
  and and_4 (and_4_out, and_2_out, j_k_ff_5_q);
  LED led_5 (.in(j_k_ff_5_q));
  D_Flip_Flop d_ff_5 (.D(j_k_ff_5_q), .clk(or_2_out), .Q(d_ff_5_q[0]));  // open: Qn, preset, reset
  T_Flip_Flop t_ff_1 (.T(and_5_out), .clk(and_5_out), .Q(t_ff_1_q));  // open: Qn, reset, preset
  and and_5 (and_5_out, d_ff_1_q[1], d_ff_5_q[0]);
  LED led_6 (.in(t_ff_1_q));
  or or_2 (or_2_out, or_3_out, or_6_out);
  Hex_Digit_Display hex_digit_display_1 (.value({{3{in_3}}, d_ff_5_q[0]}));  // open: dp
  Hex_Digit_Display hex_digit_display_2 (.value(d_ff_1_q));  // open: dp
  or or_3 (or_3_out, and_7_out, and_8_out);
  Button button_1 (.out(button_1_out));
  Clock clock_1 (.out(clock_1_out));
  Button button_2 (.out(button_2_out));
  Hex_Digit_Display hex_digit_display_3 (.value({in_6, d_ff_10_q}));  // open: dp
  Hex_Digit_Display hex_digit_display_4 (.value(d_ff_6_q));  // open: dp
  not not_1 (not_1_out, Set_Time);
  and and_6 (and_6_out, button_1_out, Set_Time);
  and and_7 (and_7_out, not_1_out, clock_1_out);
  and and_8 (and_8_out, Set_Time, button_2_out);
  or or_4 (or_4_out, and_6_out, and_7_out);
  or or_5 (or_5_out, and_8_out, and_15_out);
  J_K_Flip_Flop j_k_ff_6 (.J(in_2), .K(in_2), .clk(or_4_out), .Q(j_k_ff_6_q));  // open: Qn, preset, reset
  J_K_Flip_Flop j_k_ff_7 (.J(and_9_out), .K(j_k_ff_6_q), .clk(or_4_out), .Q(j_k_ff_7_q));  // open: Qn, preset, reset
  J_K_Flip_Flop j_k_ff_8 (.J(and_10_out), .K(and_10_out), .clk(or_4_out), .Q(j_k_ff_8_q));  // open: Qn, preset, reset
  J_K_Flip_Flop j_k_ff_9 (
    .J(and_11_out), .K(j_k_ff_6_q), .clk(or_4_out), .Q(j_k_ff_9_q), .Qn(j_k_ff_9_qn));  // open: preset, reset
  or or_6 (or_6_out, or_4_out, and_8_out);
  and and_9 (and_9_out, j_k_ff_9_qn, j_k_ff_6_q);
  and and_10 (and_10_out, j_k_ff_7_q, j_k_ff_6_q);
  and and_11 (and_11_out, j_k_ff_8_q, and_10_out);
  LED led_7 (.in(j_k_ff_6_q));
  LED led_8 (.in(j_k_ff_7_q));
  LED led_9 (.in(j_k_ff_8_q));
  LED led_10 (.in(j_k_ff_9_q));
  D_Flip_Flop d_ff_6 (.D(j_k_ff_6_q), .clk(or_6_out), .Q(d_ff_6_q[0]));  // open: Qn, preset, reset
  D_Flip_Flop d_ff_7 (.D(j_k_ff_7_q), .clk(or_6_out), .Q(d_ff_6_q[1]));  // open: Qn, preset, reset
  D_Flip_Flop d_ff_8 (.D(j_k_ff_8_q), .clk(or_6_out), .Q(d_ff_6_q[2]));  // open: Qn, preset, reset
  D_Flip_Flop d_ff_9 (.D(j_k_ff_9_q), .clk(or_6_out), .Q(d_ff_6_q[3]));  // open: Qn, preset, reset
  and and_12 (and_12_out, d_ff_6_q[0], d_ff_6_q[3]);
  J_K_Flip_Flop j_k_ff_10 (.J(in_2), .K(in_2), .clk(and_12_out), .Q(j_k_ff_10_q));  // open: Qn, preset, reset
  J_K_Flip_Flop j_k_ff_11 (
    .J(and_13_out), .K(j_k_ff_10_q), .clk(and_12_out), .Q(j_k_ff_11_q));  // open: Qn, preset, reset
  J_K_Flip_Flop j_k_ff_12 (
    .J(and_14_out), .K(j_k_ff_10_q), .clk(and_12_out), .Q(j_k_ff_12_q), .Qn(j_k_ff_12_qn));  // open: preset, reset
  and and_13 (and_13_out, j_k_ff_12_qn, j_k_ff_10_q);
  and and_14 (and_14_out, j_k_ff_11_q, j_k_ff_10_q);
  D_Flip_Flop d_ff_10 (.D(j_k_ff_10_q), .clk(or_6_out), .Q(d_ff_10_q[0]));  // open: Qn, preset, reset
  LED led_11 (.in(j_k_ff_10_q));
  D_Flip_Flop d_ff_11 (.D(j_k_ff_11_q), .clk(or_6_out), .Q(d_ff_10_q[1]));  // open: Qn, preset, reset
  LED led_12 (.in(j_k_ff_11_q));
  D_Flip_Flop d_ff_12 (.D(j_k_ff_12_q), .clk(or_6_out), .Q(d_ff_10_q[2]));  // open: Qn, preset, reset
  LED led_13 (.in(j_k_ff_12_q));
  and and_15 (and_15_out, and_12_out, and_16_out);
  and and_16 (and_16_out, d_ff_10_q[0], d_ff_10_q[2]);

  // Notes on the sheet:
  //   MOD-10-Unit column for hour
  //   Ten column for hour
  //   AM(off)-PM(on)
  //   m+
  //   clock
  //   h+
  //   MOD-10-Unit for minute
  //   Connect  minute circuit with hour circuit- +1 for hour  when minute = 59 
  //   MOD-6 - Ten column for minute 
endmodule

module stage3 (
  input  in_1,
  input  in_2,
  input  in_3
);

  wire and_1_out, and_2_out, and_3_out, and_4_out, and_5_out, clock_1_out, j_k_ff_1_q, j_k_ff_2_q,
       j_k_ff_3_q, j_k_ff_4_q, j_k_ff_5_q, or_1_out, t_ff_1_q;
  wire [0:0] d_ff_5_q;
  wire [3:0] d_ff_1_q;

  Clock clock_1 (.out(clock_1_out));
  J_K_Flip_Flop j_k_ff_1 (.J(in_2), .K(in_2), .clk(clock_1_out), .Q(j_k_ff_1_q));  // open: Qn, preset, reset
  J_K_Flip_Flop j_k_ff_2 (
    .J(j_k_ff_1_q), .K(j_k_ff_1_q), .clk(clock_1_out), .Q(j_k_ff_2_q), .reset(or_1_out));  // open: Qn, preset
  J_K_Flip_Flop j_k_ff_3 (
    .J(and_1_out), .K(and_1_out), .clk(clock_1_out), .Q(j_k_ff_3_q), .reset(or_1_out));  // open: Qn, preset
  J_K_Flip_Flop j_k_ff_4 (
    .J(and_2_out), .K(and_2_out), .clk(clock_1_out), .Q(j_k_ff_4_q), .reset(or_1_out));  // open: Qn, preset
  and and_1 (and_1_out, j_k_ff_4_q, and_2_out);
  and and_2 (and_2_out, j_k_ff_2_q, j_k_ff_1_q);
  LED led_1 (.in(j_k_ff_1_q));
  LED led_2 (.in(j_k_ff_2_q));
  LED led_3 (.in(j_k_ff_4_q));
  LED led_4 (.in(j_k_ff_3_q));
  and and_3 (and_3_out, j_k_ff_2_q, j_k_ff_3_q);
  D_Flip_Flop d_ff_1 (.D(j_k_ff_1_q), .clk(clock_1_out), .Q(d_ff_1_q[0]));  // open: Qn, preset, reset
  D_Flip_Flop d_ff_2 (.D(j_k_ff_2_q), .clk(clock_1_out), .Q(d_ff_1_q[1]));  // open: Qn, preset, reset
  or or_1 (or_1_out, and_3_out, and_4_out);
  J_K_Flip_Flop j_k_ff_5 (.J(in_2), .K(in_2), .clk(and_3_out), .Q(j_k_ff_5_q), .reset(and_4_out));  // open: Qn, preset
  D_Flip_Flop d_ff_3 (.D(j_k_ff_4_q), .clk(clock_1_out), .Q(d_ff_1_q[2]));  // open: Qn, preset, reset
  D_Flip_Flop d_ff_4 (.D(j_k_ff_3_q), .clk(clock_1_out), .Q(d_ff_1_q[3]));  // open: Qn, preset, reset
  and and_4 (and_4_out, and_2_out, j_k_ff_5_q);
  LED led_5 (.in(j_k_ff_5_q));
  D_Flip_Flop d_ff_5 (.D(j_k_ff_5_q), .clk(clock_1_out), .Q(d_ff_5_q[0]));  // open: Qn, preset, reset
  T_Flip_Flop t_ff_1 (.T(and_5_out), .clk(and_5_out), .Q(t_ff_1_q));  // open: Qn, reset, preset
  and and_5 (and_5_out, d_ff_1_q[1], d_ff_5_q[0]);
  LED led_6 (.in(t_ff_1_q));
  Hex_Digit_Display hex_digit_display_1 (.value({{3{in_1}}, d_ff_5_q[0]}));  // open: dp
  Hex_Digit_Display hex_digit_display_2 (.value(d_ff_1_q));  // open: dp

  // Notes on the sheet:
  //   MOD-10-Unit column for hour
  //   Ten column for hour
  //   AM(off)-PM(on)
endmodule

module test (
  input  Set_Time,
  input  in_2,
  input  in_3,
  input  in_4,
  input  in_5,
  input  in_6,
  input  Set_Time_2,
  input  in_8,
  input  in_9,
  input  in_10,
  input  in_11,
  input  in_12
);

  wire and_1_out, and_2_out, and_3_out, and_4_out, and_5_out, and_6_out, and_7_out, and_8_out, and_9_out,
       and_10_out, and_11_out, and_12_out, and_13_out, and_14_out, and_15_out, and_16_out, and_17_out,
       and_18_out, and_19_out, and_20_out, and_21_out, and_22_out, and_23_out, and_24_out, and_25_out,
       and_26_out, and_27_out, and_28_out, and_29_out, and_30_out, and_31_out, and_32_out, and_33_out,
       button_1_out, button_2_out, button_3_out, button_4_out, clock_1_out, clock_2_out, j_k_ff_1_q,
       j_k_ff_2_q, j_k_ff_3_q, j_k_ff_4_q, j_k_ff_5_q, j_k_ff_6_q, j_k_ff_7_q, j_k_ff_8_q, j_k_ff_9_q,
       j_k_ff_9_qn, j_k_ff_10_q, j_k_ff_11_q, j_k_ff_12_q, j_k_ff_12_qn, j_k_ff_13_q, j_k_ff_14_q,
       j_k_ff_15_q, j_k_ff_16_q, j_k_ff_17_q, j_k_ff_18_q, j_k_ff_19_q, j_k_ff_20_q, j_k_ff_21_q,
       j_k_ff_21_qn, j_k_ff_22_q, j_k_ff_23_q, j_k_ff_24_q, j_k_ff_24_qn, not_1_out, not_2_out, or_1_out,
       or_2_out, or_3_out, or_4_out, or_5_out, or_6_out, or_7_out, or_8_out, or_9_out, or_10_out, or_11_out,
       t_ff_1_q, t_ff_2_q;
  wire [0:0] d_ff_5_q, d_ff_17_q;
  wire [2:0] d_ff_10_q, d_ff_22_q;
  wire [3:0] d_ff_1_q, d_ff_6_q, d_ff_13_q, d_ff_18_q;

  J_K_Flip_Flop j_k_ff_1 (.J(in_2), .K(in_2), .clk(or_5_out), .Q(j_k_ff_1_q));  // open: Qn, preset, reset
  J_K_Flip_Flop j_k_ff_2 (
    .J(j_k_ff_1_q), .K(j_k_ff_1_q), .clk(or_5_out), .Q(j_k_ff_2_q), .reset(or_1_out));  // open: Qn, preset
  J_K_Flip_Flop j_k_ff_3 (
    .J(and_1_out), .K(and_1_out), .clk(or_5_out), .Q(j_k_ff_3_q), .reset(or_1_out));  // open: Qn, preset
  J_K_Flip_Flop j_k_ff_4 (
    .J(and_2_out), .K(and_2_out), .clk(or_5_out), .Q(j_k_ff_4_q), .reset(or_1_out));  // open: Qn, preset
  and and_1 (and_1_out, j_k_ff_4_q, and_2_out);
  and and_2 (and_2_out, j_k_ff_2_q, j_k_ff_1_q);
  LED led_1 (.in(j_k_ff_1_q));
  LED led_2 (.in(j_k_ff_2_q));
  LED led_3 (.in(j_k_ff_4_q));
  LED led_4 (.in(j_k_ff_3_q));
  and and_3 (and_3_out, j_k_ff_2_q, j_k_ff_3_q);
  D_Flip_Flop d_ff_1 (.D(j_k_ff_1_q), .clk(or_2_out), .Q(d_ff_1_q[0]));  // open: Qn, preset, reset
  D_Flip_Flop d_ff_2 (.D(j_k_ff_2_q), .clk(or_2_out), .Q(d_ff_1_q[1]));  // open: Qn, preset, reset
  or or_1 (or_1_out, and_3_out, and_4_out);
  J_K_Flip_Flop j_k_ff_5 (.J(in_2), .K(in_2), .clk(and_3_out), .Q(j_k_ff_5_q), .reset(and_4_out));  // open: Qn, preset
  D_Flip_Flop d_ff_3 (.D(j_k_ff_4_q), .clk(or_2_out), .Q(d_ff_1_q[2]));  // open: Qn, preset, reset
  D_Flip_Flop d_ff_4 (.D(j_k_ff_3_q), .clk(or_2_out), .Q(d_ff_1_q[3]));  // open: Qn, preset, reset
  and and_4 (and_4_out, and_2_out, j_k_ff_5_q);
  LED led_5 (.in(j_k_ff_5_q));
  D_Flip_Flop d_ff_5 (.D(j_k_ff_5_q), .clk(or_2_out), .Q(d_ff_5_q[0]));  // open: Qn, preset, reset
  T_Flip_Flop t_ff_1 (.T(and_5_out), .clk(and_5_out), .Q(t_ff_1_q));  // open: Qn, reset, preset
  and and_5 (and_5_out, d_ff_1_q[1], d_ff_5_q[0]);
  LED led_6 (.in(t_ff_1_q));
  or or_2 (or_2_out, or_3_out, or_6_out);
  Hex_Digit_Display hex_digit_display_1 (.value({{3{in_3}}, d_ff_5_q[0]}));  // open: dp
  Hex_Digit_Display hex_digit_display_2 (.value(d_ff_1_q));  // open: dp
  or or_3 (or_3_out, and_7_out, and_8_out);
  Button button_1 (.out(button_1_out));
  Clock clock_1 (.out(clock_1_out));
  Button button_2 (.out(button_2_out));
  Hex_Digit_Display hex_digit_display_3 (.value({in_6, d_ff_10_q}));  // open: dp
  Hex_Digit_Display hex_digit_display_4 (.value(d_ff_6_q));  // open: dp
  not not_1 (not_1_out, Set_Time);
  and and_6 (and_6_out, button_1_out, Set_Time);
  and and_7 (and_7_out, not_1_out, clock_1_out);
  and and_8 (and_8_out, Set_Time, button_2_out);
  or or_4 (or_4_out, and_6_out, and_7_out);
  or or_5 (or_5_out, and_8_out, and_15_out);
  J_K_Flip_Flop j_k_ff_6 (.J(in_2), .K(in_2), .clk(or_4_out), .Q(j_k_ff_6_q));  // open: Qn, preset, reset
  J_K_Flip_Flop j_k_ff_7 (.J(and_9_out), .K(j_k_ff_6_q), .clk(or_4_out), .Q(j_k_ff_7_q));  // open: Qn, preset, reset
  J_K_Flip_Flop j_k_ff_8 (.J(and_10_out), .K(and_10_out), .clk(or_4_out), .Q(j_k_ff_8_q));  // open: Qn, preset, reset
  J_K_Flip_Flop j_k_ff_9 (
    .J(and_11_out), .K(j_k_ff_6_q), .clk(or_4_out), .Q(j_k_ff_9_q), .Qn(j_k_ff_9_qn));  // open: preset, reset
  or or_6 (or_6_out, or_4_out, and_8_out);
  and and_9 (and_9_out, j_k_ff_9_qn, j_k_ff_6_q);
  and and_10 (and_10_out, j_k_ff_7_q, j_k_ff_6_q);
  and and_11 (and_11_out, j_k_ff_8_q, and_10_out);
  LED led_7 (.in(j_k_ff_6_q));
  LED led_8 (.in(j_k_ff_7_q));
  LED led_9 (.in(j_k_ff_8_q));
  LED led_10 (.in(j_k_ff_9_q));
  D_Flip_Flop d_ff_6 (.D(j_k_ff_6_q), .clk(or_6_out), .Q(d_ff_6_q[0]));  // open: Qn, preset, reset
  D_Flip_Flop d_ff_7 (.D(j_k_ff_7_q), .clk(or_6_out), .Q(d_ff_6_q[1]));  // open: Qn, preset, reset
  D_Flip_Flop d_ff_8 (.D(j_k_ff_8_q), .clk(or_6_out), .Q(d_ff_6_q[2]));  // open: Qn, preset, reset
  D_Flip_Flop d_ff_9 (.D(j_k_ff_9_q), .clk(or_6_out), .Q(d_ff_6_q[3]));  // open: Qn, preset, reset
  and and_12 (and_12_out, d_ff_6_q[0], d_ff_6_q[3]);
  J_K_Flip_Flop j_k_ff_10 (.J(in_2), .K(in_2), .clk(and_12_out), .Q(j_k_ff_10_q));  // open: Qn, preset, reset
  J_K_Flip_Flop j_k_ff_11 (
    .J(and_13_out), .K(j_k_ff_10_q), .clk(and_12_out), .Q(j_k_ff_11_q));  // open: Qn, preset, reset
  J_K_Flip_Flop j_k_ff_12 (
    .J(and_14_out), .K(j_k_ff_10_q), .clk(and_12_out), .Q(j_k_ff_12_q), .Qn(j_k_ff_12_qn));  // open: preset, reset
  and and_13 (and_13_out, j_k_ff_12_qn, j_k_ff_10_q);
  and and_14 (and_14_out, j_k_ff_11_q, j_k_ff_10_q);
  D_Flip_Flop d_ff_10 (.D(j_k_ff_10_q), .clk(or_6_out), .Q(d_ff_10_q[0]));  // open: Qn, preset, reset
  LED led_11 (.in(j_k_ff_10_q));
  D_Flip_Flop d_ff_11 (.D(j_k_ff_11_q), .clk(or_6_out), .Q(d_ff_10_q[1]));  // open: Qn, preset, reset
  LED led_12 (.in(j_k_ff_11_q));
  D_Flip_Flop d_ff_12 (.D(j_k_ff_12_q), .clk(or_6_out), .Q(d_ff_10_q[2]));  // open: Qn, preset, reset
  LED led_13 (.in(j_k_ff_12_q));
  and and_15 (and_15_out, and_12_out, and_16_out);
  and and_16 (and_16_out, d_ff_10_q[0], d_ff_10_q[2]);
  J_K_Flip_Flop j_k_ff_13 (.J(in_8), .K(in_8), .clk(or_11_out), .Q(j_k_ff_13_q));  // open: Qn, preset, reset
  J_K_Flip_Flop j_k_ff_14 (
    .J(j_k_ff_13_q), .K(j_k_ff_13_q), .clk(or_11_out), .Q(j_k_ff_14_q), .reset(or_7_out));  // open: Qn, preset
  J_K_Flip_Flop j_k_ff_15 (
    .J(and_17_out), .K(and_17_out), .clk(or_11_out), .Q(j_k_ff_15_q), .reset(or_7_out));  // open: Qn, preset
  J_K_Flip_Flop j_k_ff_16 (
    .J(and_18_out), .K(and_18_out), .clk(or_11_out), .Q(j_k_ff_16_q), .reset(or_7_out));  // open: Qn, preset
  and and_17 (and_17_out, j_k_ff_14_q, j_k_ff_13_q);
  and and_18 (and_18_out, j_k_ff_15_q, and_17_out);
  and and_19 (and_19_out, j_k_ff_14_q, j_k_ff_16_q);
  LED led_14 (.in(j_k_ff_13_q));
  LED led_15 (.in(j_k_ff_14_q));
  LED led_16 (.in(j_k_ff_15_q));
  LED led_17 (.in(j_k_ff_16_q));
  J_K_Flip_Flop j_k_ff_17 (
    .J(in_8), .K(in_8), .clk(and_19_out), .Q(j_k_ff_17_q), .reset(and_20_out));  // open: Qn, preset
  D_Flip_Flop d_ff_13 (.D(j_k_ff_13_q), .clk(or_8_out), .Q(d_ff_13_q[0]));  // open: Qn, preset, reset
  D_Flip_Flop d_ff_14 (.D(j_k_ff_14_q), .clk(or_8_out), .Q(d_ff_13_q[1]));  // open: Qn, preset, reset
  D_Flip_Flop d_ff_15 (.D(j_k_ff_15_q), .clk(or_8_out), .Q(d_ff_13_q[2]));  // open: Qn, preset, reset
  D_Flip_Flop d_ff_16 (.D(j_k_ff_16_q), .clk(or_8_out), .Q(d_ff_13_q[3]));  // open: Qn, preset, reset
  or or_7 (or_7_out, and_19_out, and_20_out);
  and and_20 (and_20_out, and_17_out, j_k_ff_17_q);
  LED led_18 (.in(j_k_ff_17_q));
  D_Flip_Flop d_ff_17 (.D(j_k_ff_17_q), .clk(or_8_out), .Q(d_ff_17_q[0]));  // open: Qn, preset, reset
  and and_21 (and_21_out, d_ff_13_q[1], d_ff_17_q[0]);
  T_Flip_Flop t_ff_2 (.T(and_21_out), .clk(and_21_out), .Q(t_ff_2_q));  // open: Qn, reset, preset
  LED led_19 (.in(t_ff_2_q));
  or or_8 (or_8_out, and_23_out, or_9_out);
  Hex_Digit_Display hex_digit_display_5 (.value({{3{in_9}}, d_ff_17_q[0]}));  // open: dp
  Hex_Digit_Display hex_digit_display_6 (.value(d_ff_13_q));  // open: dp
  Button button_3 (.out(button_3_out));
  Clock clock_2 (.out(clock_2_out));
  Button button_4 (.out(button_4_out));
  or or_9 (or_9_out, and_24_out, and_25_out);
  Hex_Digit_Display hex_digit_display_7 (.value({in_12, d_ff_22_q}));  // open: dp
  Hex_Digit_Display hex_digit_display_8 (.value(d_ff_18_q));  // open: dp
  not not_2 (not_2_out, Set_Time_2);
  and and_22 (and_22_out, button_3_out, Set_Time_2);
  and and_23 (and_23_out, not_2_out, clock_2_out);
  and and_24 (and_24_out, Set_Time_2, button_4_out);
  and and_25 (and_25_out, and_22_out, or_11_out);
  or or_10 (or_10_out, and_22_out, and_23_out);
  or or_11 (or_11_out, and_24_out, and_32_out);
  J_K_Flip_Flop j_k_ff_18 (.J(in_8), .K(in_8), .clk(or_10_out), .Q(j_k_ff_18_q));  // open: Qn, preset, reset
  J_K_Flip_Flop j_k_ff_19 (
    .J(and_26_out), .K(j_k_ff_18_q), .clk(or_10_out), .Q(j_k_ff_19_q));  // open: Qn, preset, reset
  J_K_Flip_Flop j_k_ff_20 (
    .J(and_27_out), .K(and_27_out), .clk(or_10_out), .Q(j_k_ff_20_q));  // open: Qn, preset, reset
  J_K_Flip_Flop j_k_ff_21 (
    .J(and_28_out), .K(j_k_ff_18_q), .clk(or_10_out), .Q(j_k_ff_21_q), .Qn(j_k_ff_21_qn));  // open: preset, reset
  and and_26 (and_26_out, j_k_ff_21_qn, j_k_ff_18_q);
  and and_27 (and_27_out, j_k_ff_19_q, j_k_ff_18_q);
  and and_28 (and_28_out, j_k_ff_20_q, and_27_out);
  LED led_20 (.in(j_k_ff_18_q));
  LED led_21 (.in(j_k_ff_19_q));
  LED led_22 (.in(j_k_ff_20_q));
  LED led_23 (.in(j_k_ff_21_q));
  D_Flip_Flop d_ff_18 (.D(j_k_ff_18_q), .clk(or_10_out), .Q(d_ff_18_q[0]));  // open: Qn, preset, reset
  D_Flip_Flop d_ff_19 (.D(j_k_ff_19_q), .clk(or_10_out), .Q(d_ff_18_q[1]));  // open: Qn, preset, reset
  D_Flip_Flop d_ff_20 (.D(j_k_ff_20_q), .clk(or_10_out), .Q(d_ff_18_q[2]));  // open: Qn, preset, reset
  D_Flip_Flop d_ff_21 (.D(j_k_ff_21_q), .clk(or_10_out), .Q(d_ff_18_q[3]));  // open: Qn, preset, reset
  and and_29 (and_29_out, d_ff_18_q[0], d_ff_18_q[3]);
  J_K_Flip_Flop j_k_ff_22 (.J(in_8), .K(in_8), .clk(and_29_out), .Q(j_k_ff_22_q));  // open: Qn, preset, reset
  J_K_Flip_Flop j_k_ff_23 (
    .J(and_30_out), .K(j_k_ff_22_q), .clk(and_29_out), .Q(j_k_ff_23_q));  // open: Qn, preset, reset
  J_K_Flip_Flop j_k_ff_24 (
    .J(and_31_out), .K(j_k_ff_22_q), .clk(and_29_out), .Q(j_k_ff_24_q), .Qn(j_k_ff_24_qn));  // open: preset, reset
  LED led_24 (.in(j_k_ff_22_q));
  and and_30 (and_30_out, j_k_ff_24_qn, j_k_ff_22_q);
  LED led_25 (.in(j_k_ff_23_q));
  and and_31 (and_31_out, j_k_ff_23_q, j_k_ff_22_q);
  LED led_26 (.in(j_k_ff_24_q));
  D_Flip_Flop d_ff_22 (.D(j_k_ff_22_q), .clk(or_10_out), .Q(d_ff_22_q[0]));  // open: Qn, preset, reset
  D_Flip_Flop d_ff_23 (.D(j_k_ff_23_q), .clk(or_10_out), .Q(d_ff_22_q[1]));  // open: Qn, preset, reset
  D_Flip_Flop d_ff_24 (.D(j_k_ff_24_q), .clk(or_10_out), .Q(d_ff_22_q[2]));  // open: Qn, preset, reset
  and and_32 (and_32_out, and_29_out, and_33_out);
  and and_33 (and_33_out, d_ff_22_q[0], d_ff_22_q[2]);

  // Notes on the sheet:
  //   MOD-10-Unit column for hour
  //   Ten column for hour
  //   AM(off)-PM(on)
  //   m+
  //   clock
  //   h+
  //   MOD-10-Unit for minute
  //   Connect  minute circuit with hour circuit- +1 for hour  when minute = 59 
  //   MOD-6 - Ten column for minute 
  //   MOD-10-Unit column for hour
  //   1
  //   2
  //   4
  //   8
  //   Ten column for hour
  //   AM(off)-PM(on)
  //   clock
  //   h+
  //   m+
  //   MOD-10-Unit for minute
  //   1
  //   2
  //   4
  //   8
  //   Connect  minute circuit with hour circuit- +1 for hour  when minute = 59 
  //   MOD-6 - Ten column for minute 
  //   1
  //   2
  //   4
endmodule

module stage2 (
  input  in_1,
  input  in_2,
  input  in_3,
  input  Set_Time
);

  wire and_1_out, and_2_out, and_3_out, and_4_out, and_5_out, and_6_out, and_7_out, and_8_out, and_9_out,
       and_10_out, button_1_out, clock_1_out, j_k_ff_6_qn, j_k_ff_7_qn, not_1_out, not_2_out, or_1_out;
  wire [2:0] j_k_ff_2_q;
  wire [3:0] j_k_ff_1_q;

  Clock clock_1 (.out(clock_1_out));
  Button button_1 (.out(button_1_out));
  not not_1 (not_1_out, Set_Time);
  and and_1 (and_1_out, clock_1_out, not_1_out);
  and and_2 (and_2_out, Set_Time, button_1_out);
  or or_1 (or_1_out, and_1_out, and_2_out);
  and and_3 (and_3_out, and_4_out, j_k_ff_7_qn);
  and and_4 (and_4_out, j_k_ff_1_q[3], not_2_out);
  J_K_Flip_Flop j_k_ff_1 (
    .J(in_3), .K(in_3), .clk(or_1_out), .Q(j_k_ff_1_q[0]), .reset(and_3_out));  // open: Qn, preset
  LED led_1 (.in(j_k_ff_1_q[0]));
  J_K_Flip_Flop j_k_ff_2 (
    .J(and_3_out), .K(and_3_out), .clk(and_3_out), .Q(j_k_ff_2_q[0]), .reset(and_10_out));  // open: Qn, preset
  not not_2 (not_2_out, j_k_ff_1_q[2]);
  LED led_2 (.in(j_k_ff_2_q[0]));
  and and_5 (and_5_out, j_k_ff_1_q[0], j_k_ff_7_qn);
  and and_6 (and_6_out, j_k_ff_2_q[0], j_k_ff_6_qn);
  J_K_Flip_Flop j_k_ff_3 (
    .J(and_5_out), .K(j_k_ff_1_q[0]), .clk(or_1_out), .Q(j_k_ff_1_q[1]), .reset(and_3_out));  // open: Qn, preset
  J_K_Flip_Flop j_k_ff_4 (
    .J(and_6_out), .K(j_k_ff_2_q[0]), .clk(and_3_out), .Q(j_k_ff_2_q[1]), .reset(and_10_out));  // open: Qn, preset
  LED led_3 (.in(j_k_ff_1_q[1]));
  and and_7 (and_7_out, j_k_ff_1_q[0], j_k_ff_1_q[1]);
  LED led_4 (.in(j_k_ff_2_q[1]));
  J_K_Flip_Flop j_k_ff_5 (
    .J(and_7_out), .K(and_7_out), .clk(or_1_out), .Q(j_k_ff_1_q[2]), .reset(and_3_out));  // open: Qn, preset
  and and_8 (and_8_out, j_k_ff_2_q[0], j_k_ff_2_q[1]);
  LED led_5 (.in(j_k_ff_1_q[2]));
  J_K_Flip_Flop j_k_ff_6 (
    .J(and_8_out), .K(j_k_ff_2_q[0]), .clk(and_3_out), .Q(j_k_ff_2_q[2]), .Qn(j_k_ff_6_qn), .reset(and_10_out));  // open: preset
  LED led_6 (.in(j_k_ff_2_q[2]));
  and and_9 (and_9_out, and_7_out, j_k_ff_1_q[2]);
  J_K_Flip_Flop j_k_ff_7 (
    .J(and_9_out), .K(j_k_ff_1_q[0]), .clk(or_1_out), .Q(j_k_ff_1_q[3]), .Qn(j_k_ff_7_qn), .reset(and_3_out));  // open: preset
  and and_10 (and_10_out, j_k_ff_2_q[2], j_k_ff_6_qn);
  LED led_7 (.in(j_k_ff_1_q[3]));
  Hex_Digit_Display hex_digit_display_1 (.value({in_1, j_k_ff_2_q}));  // open: dp
  Hex_Digit_Display hex_digit_display_2 (.value(j_k_ff_1_q));  // open: dp

  // Notes on the sheet:
  //   Clock
  //   m+
endmodule
