// Logisim project state1.circ as structural Verilog: 1 circuit, main circuit main
module main (
  input  in_1,
  input  in_2,
  input  in_3,
  input  Set_Time,
  input  in_5,
  input  in_6,
  input  in_7,
  input  in_8,
  input  in_9,
  input  in_10
);

  wire and_1_out, and_2_out, and_3_out, and_4_out, and_5_out, and_6_out, and_7_out, and_8_out, and_9_out,
       and_10_out, and_11_out, and_12_out, and_13_out, and_14_out, and_15_out, and_16_out, and_17_out,
       and_18_out, and_19_out, and_20_out, and_21_out, and_22_out, and_23_out, and_24_out, and_25_out,
       button_1_out, button_2_out, clock_1_out, clock_2_out, j_k_ff_1_q, j_k_ff_2_q, j_k_ff_3_q, j_k_ff_4_q,
       j_k_ff_4_qn, j_k_ff_5_q, j_k_ff_6_q, j_k_ff_7_q, j_k_ff_8_q, j_k_ff_9_q, j_k_ff_9_qn, j_k_ff_11_qn,
       j_k_ff_15_qn, j_k_ff_16_qn, j_k_ff_17_q, j_k_ff_18_q, j_k_ff_19_q, j_k_ff_19_qn, not_1_out, not_2_out,
       or_1_out, or_2_out, t_ff_1_q;
  wire [0:0] d_ff_5_q;
  wire [2:0] d_ff_10_q, j_k_ff_10_q;
  wire [3:0] d_ff_1_q, d_ff_6_q, j_k_ff_11_q;

  J_K_Flip_Flop j_k_ff_1 (.J(in_5), .K(in_5), .clk(or_2_out), .Q(j_k_ff_1_q));  // open: Qn, preset, reset
  J_K_Flip_Flop j_k_ff_2 (
    .J(and_1_out), .K(j_k_ff_1_q), .clk(or_2_out), .Q(j_k_ff_2_q), .reset(and_5_out));  // open: Qn, preset
  J_K_Flip_Flop j_k_ff_3 (
    .J(and_2_out), .K(and_2_out), .clk(or_2_out), .Q(j_k_ff_3_q), .reset(and_5_out));  // open: Qn, preset
  J_K_Flip_Flop j_k_ff_4 (
    .J(and_3_out), .K(j_k_ff_1_q), .clk(or_2_out), .Q(j_k_ff_4_q), .Qn(j_k_ff_4_qn), .reset(and_5_out));  // open: preset
  and and_1 (and_1_out, j_k_ff_4_qn, j_k_ff_1_q);
  and and_2 (and_2_out, j_k_ff_2_q, j_k_ff_1_q);
  and and_3 (and_3_out, j_k_ff_3_q, and_2_out);
  LED led_1 (.in(j_k_ff_1_q));
  LED led_2 (.in(j_k_ff_2_q));
  LED led_3 (.in(j_k_ff_3_q));
  LED led_4 (.in(j_k_ff_4_q));
  D_Flip_Flop d_ff_1 (.D(j_k_ff_1_q), .clk(or_1_out), .Q(d_ff_1_q[0]));  // open: Qn, preset, reset
  D_Flip_Flop d_ff_2 (.D(j_k_ff_2_q), .clk(or_1_out), .Q(d_ff_1_q[1]));  // open: Qn, preset, reset
  D_Flip_Flop d_ff_3 (.D(j_k_ff_3_q), .clk(or_1_out), .Q(d_ff_1_q[2]));  // open: Qn, preset, reset
  D_Flip_Flop d_ff_4 (.D(j_k_ff_4_q), .clk(or_1_out), .Q(d_ff_1_q[3]));  // open: Qn, preset, reset
  and and_4 (and_4_out, j_k_ff_2_q, j_k_ff_4_q);
  and and_5 (and_5_out, and_2_out, j_k_ff_5_q);
  J_K_Flip_Flop j_k_ff_5 (.J(in_5), .K(in_5), .clk(and_4_out), .Q(j_k_ff_5_q), .reset(and_5_out));  // open: Qn, preset
  LED led_5 (.in(j_k_ff_5_q));
  D_Flip_Flop d_ff_5 (.D(j_k_ff_5_q), .clk(or_1_out), .Q(d_ff_5_q[0]));  // open: Qn, preset, reset
  and and_6 (and_6_out, j_k_ff_2_q, d_ff_5_q[0]);
  T_Flip_Flop t_ff_1 (.T(and_6_out), .clk(or_1_out), .Q(t_ff_1_q));  // open: Qn, reset, preset
  Button button_1 (.out(button_1_out));
  Clock clock_1 (.out(clock_1_out));
  Button button_2 (.out(button_2_out));
  LED led_6 (.in(t_ff_1_q));
  not not_1 (not_1_out, Set_Time);
  Hex_Digit_Display hex_digit_display_1 (.value({{3{in_7}}, d_ff_5_q[0]}));  // open: dp
  Hex_Digit_Display hex_digit_display_2 (.value(d_ff_1_q));  // open: dp
  and and_7 (and_7_out, button_1_out, Set_Time);
  and and_8 (and_8_out, not_1_out, clock_1_out);
  and and_9 (and_9_out, Set_Time, button_2_out);
  Hex_Digit_Display hex_digit_display_3 (.value({in_10, d_ff_10_q}));  // open: dp
  Hex_Digit_Display hex_digit_display_4 (.value(d_ff_6_q));  // open: dp
  or or_1 (or_1_out, and_7_out, and_8_out);
  and and_10 (and_10_out, and_11_out, j_k_ff_16_qn);
  Clock clock_2 (.out(clock_2_out));
  or or_2 (or_2_out, and_9_out, and_24_out);
  and and_11 (and_11_out, j_k_ff_11_q[3], not_2_out);
  J_K_Flip_Flop j_k_ff_6 (.J(in_6), .K(in_6), .clk(or_1_out), .Q(j_k_ff_6_q));  // open: Qn, preset, reset
  J_K_Flip_Flop j_k_ff_7 (.J(and_12_out), .K(j_k_ff_6_q), .clk(or_1_out), .Q(j_k_ff_7_q));  // open: Qn, preset, reset
  J_K_Flip_Flop j_k_ff_8 (.J(and_14_out), .K(and_14_out), .clk(or_1_out), .Q(j_k_ff_8_q));  // open: Qn, preset, reset
  J_K_Flip_Flop j_k_ff_9 (
    .J(and_13_out), .K(j_k_ff_6_q), .clk(or_1_out), .Q(j_k_ff_9_q), .Qn(j_k_ff_9_qn));  // open: preset, reset
  LED led_7 (.in(j_k_ff_10_q[0]));
  J_K_Flip_Flop j_k_ff_10 (
    .J(and_10_out), .K(and_10_out), .clk(and_10_out), .Q(j_k_ff_10_q[0]), .reset(and_21_out));  // open: Qn, preset
  J_K_Flip_Flop j_k_ff_11 (
    .J(in_3), .K(in_3), .clk(clock_2_out), .Q(j_k_ff_11_q[0]), .Qn(j_k_ff_11_qn), .reset(and_10_out));  // open: preset
  and and_12 (and_12_out, j_k_ff_9_qn, j_k_ff_6_q);
  and and_13 (and_13_out, j_k_ff_8_q, and_14_out);
  not not_2 (not_2_out, j_k_ff_11_q[2]);
  LED led_8 (.in(j_k_ff_11_q[0]));
  and and_14 (and_14_out, j_k_ff_7_q, j_k_ff_6_q);
  and and_15 (and_15_out, j_k_ff_10_q[0], j_k_ff_15_qn);
  D_Flip_Flop d_ff_6 (.D(j_k_ff_6_q), .clk(or_1_out), .Q(d_ff_6_q[0]));  // open: Qn, preset, reset
  D_Flip_Flop d_ff_7 (.D(j_k_ff_7_q), .clk(or_1_out), .Q(d_ff_6_q[1]));  // open: Qn, preset, reset
  D_Flip_Flop d_ff_8 (.D(j_k_ff_8_q), .clk(or_1_out), .Q(d_ff_6_q[2]));  // open: Qn, preset, reset
  D_Flip_Flop d_ff_9 (.D(j_k_ff_9_q), .clk(or_1_out), .Q(d_ff_6_q[3]));  // open: Qn, preset, reset
  J_K_Flip_Flop j_k_ff_12 (
    .J(and_15_out), .K(j_k_ff_10_q[0]), .clk(and_10_out), .Q(j_k_ff_10_q[1]), .reset(and_21_out));  // open: Qn, preset
  and and_16 (and_16_out, j_k_ff_11_q[0], j_k_ff_16_qn);
  J_K_Flip_Flop j_k_ff_13 (
    .J(and_16_out), .K(j_k_ff_11_q[0]), .clk(clock_2_out), .Q(j_k_ff_11_q[1]), .reset(and_10_out));  // open: Qn, preset
  LED led_9 (.in(j_k_ff_10_q[1]));
  LED led_10 (.in(j_k_ff_11_q[1]));
  LED led_11 (.in(d_ff_6_q[0]));
  LED led_12 (.in(d_ff_6_q[1]));
  LED led_13 (.in(d_ff_6_q[2]));
  LED led_14 (.in(d_ff_6_q[3]));
  and and_17 (and_17_out, j_k_ff_11_q[0], j_k_ff_11_q[1]);
  and and_18 (and_18_out, j_k_ff_10_q[0], j_k_ff_10_q[1]);
  J_K_Flip_Flop j_k_ff_14 (
    .J(and_17_out), .K(and_17_out), .clk(clock_2_out), .Q(j_k_ff_11_q[2]), .reset(and_10_out));  // open: Qn, preset
  and and_19 (and_19_out, d_ff_6_q[3], d_ff_6_q[0]);
  LED led_15 (.in(j_k_ff_10_q[2]));
  J_K_Flip_Flop j_k_ff_15 (
    .J(and_18_out), .K(j_k_ff_10_q[0]), .clk(and_10_out), .Q(j_k_ff_10_q[2]), .Qn(j_k_ff_15_qn),
    .reset(and_21_out));  // open: preset
  LED led_16 (.in(j_k_ff_11_q[2]));
  and and_20 (and_20_out, and_17_out, j_k_ff_11_q[2]);
  and and_21 (and_21_out, j_k_ff_10_q[2], j_k_ff_15_qn);
  J_K_Flip_Flop j_k_ff_16 (
    .J(and_20_out), .K(j_k_ff_11_q[0]), .clk(clock_2_out), .Q(j_k_ff_11_q[3]), .Qn(j_k_ff_16_qn),
    .reset(and_10_out));  // open: preset
  Hex_Digit_Display hex_digit_display_5 (.value({in_1, j_k_ff_10_q}));  // open: dp
  LED led_17 (.in(j_k_ff_11_q[3]));
  Hex_Digit_Display hex_digit_display_6 (.value(j_k_ff_11_q));  // open: dp
  J_K_Flip_Flop j_k_ff_17 (
    .J(and_19_out), .K(and_19_out), .clk(and_19_out), .Q(j_k_ff_17_q));  // open: Qn, preset, reset
  J_K_Flip_Flop j_k_ff_18 (
    .J(and_22_out), .K(j_k_ff_17_q), .clk(and_19_out), .Q(j_k_ff_18_q));  // open: Qn, preset, reset
  J_K_Flip_Flop j_k_ff_19 (
    .J(and_23_out), .K(j_k_ff_17_q), .clk(and_19_out), .Q(j_k_ff_19_q), .Qn(j_k_ff_19_qn));  // open: preset, reset
  and and_22 (and_22_out, j_k_ff_19_qn, j_k_ff_17_q);
  and and_23 (and_23_out, j_k_ff_18_q, j_k_ff_17_q);
  D_Flip_Flop d_ff_10 (.D(j_k_ff_17_q), .clk(or_1_out), .Q(d_ff_10_q[0]));  // open: Qn, preset, reset
  D_Flip_Flop d_ff_11 (.D(j_k_ff_18_q), .clk(or_1_out), .Q(d_ff_10_q[1]));  // open: Qn, preset, reset
  D_Flip_Flop d_ff_12 (.D(j_k_ff_19_q), .clk(or_1_out), .Q(d_ff_10_q[2]));  // open: Qn, preset, reset
  and and_24 (and_24_out, and_19_out, and_25_out);
  and and_25 (and_25_out, d_ff_10_q[0], d_ff_10_q[2]);

  // Notes on the sheet:
  //   Set Time
  //   Set Time
  //   Clock
  //   m+
  //   Clock
  //   h+
  //   AM(off)-PM(on)
  //   MOD-10
endmodule
