// Logisim project state3.circ as structural Verilog: 1 circuit, main circuit main
module main (
  input  in_1,
  input  in_2,
  input  in_3,
  input  in_4,
  input  in_5,
  input  in_6
);

  wire and_1_out, and_2_out, and_3_out, and_4_out, and_5_out, and_6_out, and_7_out, and_8_out, and_9_out,
       button_1_out, clock_1_out, j_k_ff_5_qn, not_1_out, not_2_out, or_1_out, t_ff_1_q;
  wire [0:0] j_k_ff_1_q;
  wire [3:0] j_k_ff_2_q;

  Button button_1 (.out(button_1_out));
  Clock clock_1 (.out(clock_1_out));
  not not_1 (not_1_out, in_6);
  and and_1 (and_1_out, button_1_out, in_6);
  and and_2 (and_2_out, not_1_out, clock_1_out);
  or or_1 (or_1_out, and_1_out, and_2_out);
  and and_3 (and_3_out, and_4_out, j_k_ff_5_qn);
  and and_4 (and_4_out, j_k_ff_2_q[3], not_2_out);
  J_K_Flip_Flop j_k_ff_1 (
    .J(in_5), .K(in_5), .clk(and_3_out), .Q(j_k_ff_1_q[0]), .reset(and_9_out));  // open: Qn, preset
  J_K_Flip_Flop j_k_ff_2 (.J(in_5), .K(in_5), .clk(or_1_out), .Q(j_k_ff_2_q[0]));  // open: Qn, preset, reset
  LED led_1 (.in(j_k_ff_1_q[0]));
  LED led_2 (.in(j_k_ff_2_q[0]));
  and and_5 (and_5_out, j_k_ff_2_q[0], j_k_ff_5_qn);
  and and_6 (and_6_out, j_k_ff_1_q[0], j_k_ff_2_q[0]);
  J_K_Flip_Flop j_k_ff_3 (
    .J(and_5_out), .K(j_k_ff_2_q[0]), .clk(or_1_out), .Q(j_k_ff_2_q[1]), .reset(and_9_out));  // open: Qn, preset
  LED led_3 (.in(j_k_ff_2_q[1]));
  T_Flip_Flop t_ff_1 (.T(and_6_out), .clk(or_1_out), .Q(t_ff_1_q));  // open: Qn, reset, preset
  and and_7 (and_7_out, j_k_ff_2_q[0], j_k_ff_2_q[1]);
  LED led_4 (.in(t_ff_1_q));
  not not_2 (not_2_out, j_k_ff_2_q[2]);
  J_K_Flip_Flop j_k_ff_4 (
    .J(and_7_out), .K(and_7_out), .clk(or_1_out), .Q(j_k_ff_2_q[2]), .reset(and_9_out));  // open: Qn, preset
  LED led_5 (.in(j_k_ff_2_q[2]));
  and and_8 (and_8_out, and_7_out, j_k_ff_2_q[2]);
  J_K_Flip_Flop j_k_ff_5 (
    .J(and_8_out), .K(j_k_ff_2_q[0]), .clk(or_1_out), .Q(j_k_ff_2_q[3]), .Qn(j_k_ff_5_qn), .reset(and_9_out));  // open: preset
  LED led_6 (.in(j_k_ff_2_q[3]));
  Hex_Digit_Display hex_digit_display_1 (.value({in_1, in_2, in_3, j_k_ff_1_q[0]}));  // open: dp
  Hex_Digit_Display hex_digit_display_2 (.value(j_k_ff_2_q));  // open: dp
  and and_9 (and_9_out, j_k_ff_1_q[0], and_7_out);
endmodule
