// Logisim project Half_adder.circ as structural Verilog: 1 circuit, main circuit main
module main (
  input  pin_1,
  input  pin2
);

  wire and_1_out, xor_1_out;

  xor xor_1 (xor_1_out, pin_1, pin2);
  and and_1 (and_1_out, pin_1, pin2);
  LED led_1 (.in(xor_1_out));
  LED led_2 (.in(and_1_out));

  // Notes on the sheet:
  //   Sum
  //   Co
endmodule
