// Logisim project NAND_gate.circ as structural Verilog: 1 circuit, main circuit main
module main (
  input  pin1,
  input  in_2
);

  wire nand_1_out;

  nand nand_1 (nand_1_out, pin1, in_2);
  LED led_1 (.in(nand_1_out));

  // Notes on the sheet:
  //   pin2
  //   output
endmodule
