// Logisim project andgate.circ as structural Verilog: 1 circuit, main circuit main
module main (
  input  pin1,
  input  pin2
);

  wire and_1_out;

  buf and_1 (and_1_out, pin2);  // AND_Gate
  LED led_1 (.in(and_1_out));

  // Notes on the sheet:
  //   output
endmodule
