// Logisim project dflipflop.circ as structural Verilog: 1 circuit, main circuit main
module main (
  input  pin
);

  wire and_1_out, and_2_out, clock_1_out, nor_1_out, nor_2_out, not_1_out;

  Clock clock_1 (.out(clock_1_out));
  not not_1 (not_1_out, pin);
  buf and_1 (and_1_out, not_1_out);  // AND_Gate
  buf and_2 (and_2_out, pin);  // AND_Gate
  nor nor_1 (nor_1_out, and_1_out, nor_2_out);
  nor nor_2 (nor_2_out, and_2_out, nor_1_out);
  LED led_1 (.in(nor_1_out));
  LED led_2 (.in(nor_2_out));

  // Notes on the sheet:
  //   clock
  //   Q
  //   Q'
endmodule
