// Logisim project countuo_down.circ as structural Verilog: 1 circuit, main circuit main
module main (
  input  in_1,
  input  in_2,
  input  Enable,
  input  CLR
);

  wire clock_1_out, clock_2_out, j_k_ff_1_q, j_k_ff_2_qn, j_k_ff_3_q, j_k_ff_4_q, j_k_ff_4_qn, j_k_ff_5_q,
       j_k_ff_5_qn, j_k_ff_6_q;

  Clock clock_1 (.out(clock_1_out));
  Clock clock_2 (.out(clock_2_out));
  J_K_Flip_Flop #(.trigger("falling")) j_k_ff_1 (
    .J(in_1), .K(in_1), .clk(j_k_ff_3_q), .Q(j_k_ff_1_q), .reset(in_2));  // open: Qn, preset
  J_K_Flip_Flop #(.trigger("falling")) j_k_ff_2 (
    .J(Enable), .K(Enable), .clk(j_k_ff_4_q), .Qn(j_k_ff_2_qn), .reset(CLR));  // open: Q, preset
  LED led_1 (.in(j_k_ff_1_q));
  LED led_2 (.in(j_k_ff_2_qn));
  J_K_Flip_Flop #(.trigger("falling")) j_k_ff_3 (
    .J(in_1), .K(in_1), .clk(j_k_ff_6_q), .Q(j_k_ff_3_q), .reset(in_2));  // open: Qn, preset
  J_K_Flip_Flop #(.trigger("falling")) j_k_ff_4 (
    .J(Enable), .K(Enable), .clk(j_k_ff_5_q), .Q(j_k_ff_4_q), .Qn(j_k_ff_4_qn), .reset(CLR));  // open: preset
  LED led_3 (.in(j_k_ff_3_q));
  J_K_Flip_Flop #(.trigger("falling")) j_k_ff_5 (
    .J(Enable), .K(Enable), .clk(clock_2_out), .Q(j_k_ff_5_q), .Qn(j_k_ff_5_qn), .reset(CLR));  // open: preset
  LED led_4 (.in(j_k_ff_4_qn));
  J_K_Flip_Flop #(.trigger("falling")) j_k_ff_6 (
    .J(in_1), .K(in_1), .clk(clock_1_out), .Q(j_k_ff_6_q), .reset(in_2));  // open: Qn, preset
  LED led_5 (.in(j_k_ff_5_qn));
  LED led_6 (.in(j_k_ff_6_q));

  // Notes on the sheet:
  //   Enable
  //   Clock
  //   CLR
  //   Clock
  //   Q3-4
  //   Q3-4
  //   Q2-2
  //   Q2-2
  //   Q1-1
  //   Q1-1
endmodule
