// Logisim project mod6.circ as structural Verilog: 1 circuit, main circuit main
module main (
  input  Enable,
  input  in_2,
  input  enable_2,
  input  in_4
);

  wire and_1_out, and_2_out, and_3_out, and_4_out, clock_1_out, clock_2_out, j_k_ff_1_q, j_k_ff_3_q,
       j_k_ff_5_q;
  wire [2:0] d_ff_1_q, j_k_ff_2_q;

  Clock clock_1 (.out(clock_1_out));
  Clock clock_2 (.out(clock_2_out));
  J_K_Flip_Flop j_k_ff_1 (
    .J(Enable), .K(Enable), .clk(clock_1_out), .Q(j_k_ff_1_q), .reset(and_2_out));  // open: Qn, preset
  D_Flip_Flop d_ff_1 (.D(j_k_ff_1_q), .clk(clock_1_out), .Q(d_ff_1_q[0]));  // open: Qn, preset, reset
  LED led_1 (.in(j_k_ff_1_q));
  J_K_Flip_Flop #(.trigger("falling")) j_k_ff_2 (
    .J(enable_2), .K(enable_2), .clk(clock_2_out), .Q(j_k_ff_2_q[0]), .reset(and_4_out));  // open: Qn, preset
  J_K_Flip_Flop j_k_ff_3 (
    .J(j_k_ff_1_q), .K(j_k_ff_1_q), .clk(clock_1_out), .Q(j_k_ff_3_q), .reset(and_2_out));  // open: Qn, preset
  LED led_2 (.in(j_k_ff_2_q[0]));
  LED led_3 (.in(j_k_ff_3_q));
  D_Flip_Flop d_ff_2 (.D(j_k_ff_3_q), .clk(clock_1_out), .Q(d_ff_1_q[1]));  // open: Qn, preset, reset
  J_K_Flip_Flop #(.trigger("falling")) j_k_ff_4 (
    .J(j_k_ff_2_q[0]), .K(j_k_ff_2_q[0]), .clk(clock_2_out), .Q(j_k_ff_2_q[1]), .reset(and_4_out));  // open: Qn, preset
  and and_1 (and_1_out, j_k_ff_1_q, j_k_ff_3_q);
  J_K_Flip_Flop j_k_ff_5 (
    .J(and_1_out), .K(and_1_out), .clk(clock_1_out), .Q(j_k_ff_5_q), .reset(and_2_out));  // open: Qn, preset
  LED led_4 (.in(j_k_ff_2_q[1]));
  LED led_5 (.in(j_k_ff_5_q));
  D_Flip_Flop d_ff_3 (.D(j_k_ff_5_q), .clk(clock_1_out), .Q(d_ff_1_q[2]));  // open: Qn, preset, reset
  and and_2 (and_2_out, j_k_ff_5_q, j_k_ff_3_q);
  and and_3 (and_3_out, j_k_ff_2_q[0], j_k_ff_2_q[1]);
  J_K_Flip_Flop #(.trigger("falling")) j_k_ff_6 (
    .J(and_3_out), .K(and_3_out), .clk(clock_2_out), .Q(j_k_ff_2_q[2]), .reset(and_4_out));  // open: Qn, preset
  LED led_6 (.in(j_k_ff_2_q[2]));
  Hex_Digit_Display hex_digit_display_1 (.value({in_2, d_ff_1_q}));  // open: dp
  and and_4 (and_4_out, j_k_ff_2_q[1], j_k_ff_2_q[2]);
  Hex_Digit_Display hex_digit_display_2 (.value({in_4, j_k_ff_2_q}));  // open: dp

  // Notes on the sheet:
  //   Clock
  //   clock
  //   Q3
  //   Q2
  //   Q1
endmodule
