// Logisim project lab4.circ as structural Verilog: 1 circuit, main circuit main
module main (
  input  Data_In,
  input  CLR,
  input  Mode_control,
  input  in_4,
  input  Din,
  input  CLR_2,
  input  Mode_control_2,
  input  in_8,
  input  Din_2,
  input  CLR_3,
  input  in_11,
  input  in_12,
  input  Mode_control_3,
  input  Din_3,
  input  CLR_4,
  input  in_16,
  input  Mode_control_4,
  input  in_18,
  input  CLR_5,
  input  in_20
);

  wire and_1_out, and_2_out, and_3_out, and_4_out, and_5_out, and_6_out, and_7_out, and_8_out, and_9_out,
       and_10_out, and_11_out, and_12_out, and_13_out, and_14_out, and_15_out, and_16_out, and_17_out,
       and_18_out, and_19_out, and_20_out, and_21_out, and_22_out, and_23_out, and_24_out, and_25_out,
       and_26_out, and_27_out, and_28_out, and_29_out, and_30_out, and_31_out, and_32_out, and_33_out,
       and_34_out, and_35_out, and_36_out, and_37_out, and_38_out, and_39_out, and_40_out, and_41_out,
       and_42_out, and_43_out, and_44_out, and_45_out, and_46_out, and_47_out, and_48_out, clock_1_out,
       clock_2_out, clock_3_out, clock_4_out, clock_5_out, d_ff_1_q, d_ff_2_q, d_ff_3_q, d_ff_4_q, d_ff_5_q,
       d_ff_6_q, d_ff_7_q, d_ff_8_q, d_ff_9_q, d_ff_10_q, d_ff_11_q, d_ff_12_q, d_ff_13_q, d_ff_14_q,
       d_ff_15_q, d_ff_16_q, d_ff_17_q, d_ff_18_q, d_ff_19_q, d_ff_20_q, d_ff_21_q, d_ff_22_q, d_ff_23_q,
       d_ff_24_q, d_ff_25_q, d_ff_26_q, d_ff_27_q, not_1_out, not_2_out, not_3_out, not_4_out, not_5_out,
       not_6_out, not_7_out, not_8_out, not_9_out, or_1_out, or_2_out, or_3_out, or_4_out, or_5_out,
       or_6_out, or_7_out, or_8_out, or_9_out, or_10_out, or_11_out, or_12_out, or_13_out, or_14_out,
       or_15_out, or_16_out, or_17_out;

  Clock clock_1 (.out(clock_1_out));
  not not_1 (not_1_out, Mode_control);
  Clock clock_2 (.out(clock_2_out));
  Clock clock_3 (.out(clock_3_out));
  not not_2 (not_2_out, in_16);
  Clock clock_4 (.out(clock_4_out));
  not not_3 (not_3_out, in_20);
  and and_1 (and_1_out, Din, Mode_control);
  or or_1 (or_1_out, and_1_out, and_3_out);
  not not_4 (not_4_out, Mode_control_2);
  Clock clock_5 (.out(clock_5_out));
  not not_5 (not_5_out, in_12);
  and and_2 (and_2_out, clock_3_out, not_2_out);
  D_Flip_Flop d_ff_1 (.D(Data_In), .clk(clock_1_out), .Q(d_ff_1_q), .reset(CLR));  // open: Qn, preset
  LED led_1 (.in(d_ff_1_q));
  and and_3 (and_3_out, not_1_out, d_ff_8_q);
  D_Flip_Flop d_ff_2 (.D(or_1_out), .clk(clock_2_out), .Q(d_ff_2_q), .reset(CLR_2));  // open: Qn, preset
  and and_4 (and_4_out, Din_2, Mode_control_2);
  not not_6 (not_6_out, Mode_control_3);
  and and_5 (and_5_out, not_9_out, Mode_control_3);
  not not_7 (not_7_out, Mode_control_4);
  and and_6 (and_6_out, clock_4_out, not_3_out);
  D_Flip_Flop d_ff_3 (.D(d_ff_1_q), .clk(clock_1_out), .Q(d_ff_3_q), .reset(CLR));  // open: Qn, preset
  or or_2 (or_2_out, and_4_out, and_12_out);
  D_Flip_Flop d_ff_4 (.D(or_2_out), .clk(clock_5_out), .Q(d_ff_4_q), .reset(CLR_3));  // open: Qn, preset
  and and_7 (and_7_out, in_12, in_11);
  and and_8 (and_8_out, in_11, not_5_out);
  and and_9 (and_9_out, not_6_out, d_ff_10_q);
  or or_3 (or_3_out, and_5_out, and_9_out);
  D_Flip_Flop d_ff_5 (.D(or_3_out), .clk(and_2_out), .Q(d_ff_5_q), .reset(CLR_4));  // open: Qn, preset
  and and_10 (and_10_out, not_8_out, Mode_control_4);
  or or_4 (or_4_out, and_10_out, and_13_out);
  D_Flip_Flop d_ff_6 (.D(or_4_out), .clk(and_6_out), .Q(d_ff_6_q), .reset(CLR_5));  // open: Qn, preset
  LED led_2 (.in(d_ff_3_q));
  and and_11 (and_11_out, d_ff_2_q, Mode_control);
  LED led_3 (.in(d_ff_2_q));
  and and_12 (and_12_out, not_4_out, d_ff_9_q);
  LED led_4 (.in(d_ff_4_q));
  LED led_5 (.in(and_7_out));
  LED led_6 (.in(and_8_out));
  and and_13 (and_13_out, not_7_out, d_ff_11_q);
  D_Flip_Flop d_ff_7 (.D(d_ff_3_q), .clk(clock_1_out), .Q(d_ff_7_q), .reset(CLR));  // open: Qn, preset
  or or_5 (or_5_out, and_11_out, and_16_out);
  and and_14 (and_14_out, d_ff_5_q, not_2_out);
  LED led_7 (.in(and_14_out));
  and and_15 (and_15_out, d_ff_6_q, not_3_out);
  LED led_8 (.in(d_ff_7_q));
  and and_16 (and_16_out, not_1_out, d_ff_14_q);
  D_Flip_Flop d_ff_8 (.D(or_5_out), .clk(clock_2_out), .Q(d_ff_8_q), .reset(CLR_2));  // open: Qn, preset
  and and_17 (and_17_out, d_ff_4_q, Mode_control_2);
  and and_18 (and_18_out, d_ff_5_q, Mode_control_3);
  or or_6 (or_6_out, and_18_out, and_20_out);
  not not_8 (not_8_out, in_18);
  and and_19 (and_19_out, d_ff_6_q, Mode_control_4);
  or or_7 (or_7_out, and_17_out, and_22_out);
  D_Flip_Flop d_ff_9 (.D(or_7_out), .clk(clock_5_out), .Q(d_ff_9_q), .reset(CLR_3));  // open: Qn, preset
  and and_20 (and_20_out, not_6_out, d_ff_16_q);
  D_Flip_Flop d_ff_10 (.D(or_6_out), .clk(and_2_out), .Q(d_ff_10_q), .reset(CLR_4));  // open: Qn, preset
  or or_8 (or_8_out, and_19_out, and_23_out);
  D_Flip_Flop d_ff_11 (.D(or_8_out), .clk(and_6_out), .Q(d_ff_11_q), .reset(CLR_5));  // open: Qn, preset
  D_Flip_Flop d_ff_12 (.D(and_15_out), .clk(and_6_out), .Q(d_ff_12_q), .reset(CLR_5));  // open: Qn, preset
  D_Flip_Flop d_ff_13 (.D(d_ff_7_q), .clk(clock_1_out), .Q(d_ff_13_q), .reset(CLR));  // open: Qn, preset
  and and_21 (and_21_out, d_ff_8_q, Mode_control);
  LED led_9 (.in(d_ff_8_q));
  and and_22 (and_22_out, not_4_out, in_8);
  LED led_10 (.in(d_ff_9_q));
  and and_23 (and_23_out, not_7_out, d_ff_17_q);
  LED led_11 (.in(d_ff_13_q));
  and and_24 (and_24_out, not_1_out, d_ff_19_q);
  or or_9 (or_9_out, and_21_out, and_24_out);
  D_Flip_Flop d_ff_14 (.D(or_9_out), .clk(clock_2_out), .Q(d_ff_14_q), .reset(CLR_2));  // open: Qn, preset
  and and_25 (and_25_out, d_ff_10_q, Mode_control_3);
  and and_26 (and_26_out, d_ff_10_q, not_2_out);
  LED led_12 (.in(and_26_out));
  LED led_13 (.in(d_ff_12_q));
  D_Flip_Flop d_ff_15 (.D(d_ff_13_q), .clk(clock_1_out), .Q(d_ff_15_q), .reset(CLR));  // open: Qn, preset
  or or_10 (or_10_out, and_25_out, and_30_out);
  D_Flip_Flop d_ff_16 (.D(or_10_out), .clk(and_2_out), .Q(d_ff_16_q), .reset(CLR_4));  // open: Qn, preset
  and and_27 (and_27_out, d_ff_11_q, Mode_control_4);
  and and_28 (and_28_out, d_ff_11_q, not_3_out);
  LED led_14 (.in(d_ff_15_q));
  and and_29 (and_29_out, d_ff_14_q, Mode_control);
  LED led_15 (.in(d_ff_14_q));
  and and_30 (and_30_out, not_6_out, d_ff_20_q);
  and and_31 (and_31_out, not_7_out, d_ff_21_q);
  or or_11 (or_11_out, and_27_out, and_31_out);
  D_Flip_Flop d_ff_17 (.D(or_11_out), .clk(and_6_out), .Q(d_ff_17_q), .reset(CLR_5));  // open: Qn, preset
  D_Flip_Flop d_ff_18 (.D(and_28_out), .clk(and_6_out), .Q(d_ff_18_q), .reset(CLR_5));  // open: Qn, preset
  or or_12 (or_12_out, and_29_out, and_34_out);
  D_Flip_Flop d_ff_19 (.D(or_12_out), .clk(clock_2_out), .Q(d_ff_19_q), .reset(CLR_2));  // open: Qn, preset
  and and_32 (and_32_out, d_ff_16_q, Mode_control_3);
  and and_33 (and_33_out, d_ff_16_q, not_2_out);
  LED led_16 (.in(d_ff_18_q));
  and and_34 (and_34_out, not_1_out, d_ff_22_q);
  or or_13 (or_13_out, and_32_out, and_38_out);
  LED led_17 (.in(and_33_out));
  and and_35 (and_35_out, d_ff_17_q, Mode_control_4);
  and and_36 (and_36_out, d_ff_17_q, not_3_out);
  and and_37 (and_37_out, d_ff_19_q, Mode_control);
  LED led_18 (.in(d_ff_19_q));
  and and_38 (and_38_out, not_6_out, d_ff_24_q);
  D_Flip_Flop d_ff_20 (.D(or_13_out), .clk(and_2_out), .Q(d_ff_20_q), .reset(CLR_4));  // open: Qn, preset
  and and_39 (and_39_out, not_7_out, d_ff_25_q);
  or or_14 (or_14_out, and_35_out, and_39_out);
  D_Flip_Flop d_ff_21 (.D(or_14_out), .clk(and_6_out), .Q(d_ff_21_q), .reset(CLR_5));  // open: Qn, preset
  or or_15 (or_15_out, and_37_out, and_40_out);
  D_Flip_Flop d_ff_22 (.D(or_15_out), .clk(clock_2_out), .Q(d_ff_22_q), .reset(CLR_2));  // open: Qn, preset
  not not_9 (not_9_out, Din_3);
  D_Flip_Flop d_ff_23 (.D(and_36_out), .clk(and_6_out), .Q(d_ff_23_q), .reset(CLR_5));  // open: Qn, preset
  and and_40 (and_40_out, not_1_out, in_4);
  LED led_19 (.in(d_ff_22_q));
  and and_41 (and_41_out, d_ff_20_q, Mode_control_3);
  or or_16 (or_16_out, and_41_out, and_43_out);
  and and_42 (and_42_out, d_ff_21_q, Mode_control_4);
  LED led_20 (.in(d_ff_23_q));
  and and_43 (and_43_out, not_6_out, Din_3);
  D_Flip_Flop d_ff_24 (.D(or_16_out), .clk(and_2_out), .Q(d_ff_24_q), .reset(CLR_4));  // open: Qn, preset
  and and_44 (and_44_out, d_ff_20_q, not_2_out);
  or or_17 (or_17_out, and_42_out, and_45_out);
  D_Flip_Flop d_ff_25 (.D(or_17_out), .clk(and_6_out), .Q(d_ff_25_q), .reset(CLR_5));  // open: Qn, preset
  LED led_21 (.in(and_44_out));
  and and_45 (and_45_out, not_7_out, in_18);
  and and_46 (and_46_out, d_ff_21_q, not_3_out);
  D_Flip_Flop d_ff_26 (.D(and_46_out), .clk(and_6_out), .Q(d_ff_26_q), .reset(CLR_5));  // open: Qn, preset
  and and_47 (and_47_out, d_ff_24_q, not_2_out);
  LED led_22 (.in(and_47_out));
  and and_48 (and_48_out, d_ff_25_q, not_3_out);
  LED led_23 (.in(d_ff_26_q));
  D_Flip_Flop d_ff_27 (.D(and_48_out), .clk(and_6_out), .Q(d_ff_27_q), .reset(CLR_5));  // open: Qn, preset
  LED led_24 (.in(d_ff_27_q));

  // Notes on the sheet:
  //   Clk 
  //   CLK
  //   CLK
  //   2-bit encoder 
  //   Bidirectional Shift Register
  //   Shift Register 
endmodule
